// Digital circuit 4-bit register file.dig as structural Verilog
module _4_bit_register_file (
  input  clk,
  input  [1:0] Read_Register_1,
  input  [1:0] Read_Register_2,
  input  [7:0] Control_signals,
  input  [3:0] Write_data,
  input  [1:0] Write_register,
  output [3:0] Read_data_1,
  output [3:0] Read_data_2
);

  wire [3:0] demultiplexer_1_out_0, demultiplexer_1_out_1, demultiplexer_1_out_2, demultiplexer_1_out_3,
       R0_p4, R1_p4, R2_p4, R3_p4;

  Demultiplexer #(.Selector_Bits(2), .Bits(4)) demultiplexer_1 (
    .sel(Write_register), .in(Write_data), .out_0(demultiplexer_1_out_0), .out_1(demultiplexer_1_out_1),
    .out_2(demultiplexer_1_out_2), .out_3(demultiplexer_1_out_3));
  // register R0: pin names not known; wires that end beside it: clk, demultiplexer_1_out_0, Control_signals[1:0], R0_p4
  // register R1: pin names not known; wires that end beside it: clk, demultiplexer_1_out_1, Control_signals[3:2], R1_p4
  // register R2: pin names not known; wires that end beside it: clk, demultiplexer_1_out_2, Control_signals[5:4], R2_p4
  // register R3: pin names not known; wires that end beside it: clk, demultiplexer_1_out_3, Control_signals[7:6], R3_p4
  Multiplexer #(.Selector_Bits(2), .Bits(4)) multiplexer_1 (
    .sel(Read_Register_1), .in_0(R0_p4), .in_1(R1_p4), .in_2(R2_p4), .in_3(R3_p4), .out(Read_data_1));
  Multiplexer #(.Selector_Bits(2), .Bits(4)) multiplexer_2 (
    .sel(Read_Register_2), .in_0(R0_p4), .in_1(R1_p4), .in_2(R2_p4), .in_3(R3_p4), .out(Read_data_2));

  // Notes on the sheet:
  //   Control_signals: 2-bit for each of the four registers. depending on what 
  //   are setting 00,01,11,10.. so based on these operations, what 
  //   will we perform?
  //   Control signal
  //   Write_data: Write Data
  //   Write_register: Write register
endmodule
