// Digital circuit Register type .dig as structural Verilog
module Register_type (
  input  Clk,
  output [4:0] S,
  output IR_HI_WRITE,
  output IR_LOW_WRITE,
  output Write_back,
  output Pci
);

  D_FF #(.Default(1)) IF_1 (.D(S[4]), .C(Clk), .Q(IR_HI_WRITE));  // open: nQ
  D_FF IF_2 (.D(IR_HI_WRITE), .C(Clk), .Q(IR_LOW_WRITE));  // open: nQ
  D_FF Decode (.D(IR_LOW_WRITE), .C(Clk), .Q(S[2]));  // open: nQ
  D_FF Execute (.D(S[2]), .C(Clk), .Q(S[3]));  // open: nQ
  or or_1 (Pci, IR_HI_WRITE, S[4]);
  D_FF u_Write_back (.D(S[3]), .C(Clk), .Q(S[4]));  // open: nQ

  assign S[1:0] = {IR_LOW_WRITE, IR_HI_WRITE};
  assign Write_back = S[4];

  // Notes on the sheet:
  //   S: states
  //   Pci: Program increment
endmodule
