// Digital circuit pc counter.dig as structural Verilog
module pc_counter (
  input  clock,
  input  [3:0] Input,
  input  [1:0] Store_Clear_Load__inc,
  input  [3:0] Const,
  output [3:0] Output
);

  wire [3:0] adder_s, multiplexer_1_out;

  Add #(.Bits(4)) adder (.a(Output), .b(Const), .c_i(1'b0), .s(adder_s));  // open: c_o
  Multiplexer #(.Selector_Bits(2), .Bits(4)) multiplexer_1 (
    .sel(Store_Clear_Load__inc), .in_0(4'b0000), .in_1(Input), .in_2(Output), .in_3(adder_s),
    .out(multiplexer_1_out));
  D_FF d_ff_1 (.D(multiplexer_1_out[3]), .C(clock), .Q(Output[3]));  // open: nQ
  D_FF d_ff_2 (.D(multiplexer_1_out[2]), .C(clock), .Q(Output[2]));  // open: nQ
  D_FF d_ff_3 (.D(multiplexer_1_out[1]), .C(clock), .Q(Output[1]));  // open: nQ
  D_FF d_ff_4 (.D(multiplexer_1_out[0]), .C(clock), .Q(Output[0]));  // open: nQ

  // Notes on the sheet:
  //   Store_Clear_Load__inc: 0 -> clear
  //   1 -> store input
  //   2 -> load
  //   3 -> set F/, default 1
  //   Const: default 1
endmodule
